# Fritzing sketch RFClicker (saved by Fritzing 0.9.4)
breadboards: 1

parts:
  RFduinoSMD1 = RFduino SMD
  LED1 = LED - 5mm [color="Red (633nm)" package="5 mm [THT]"]
  R1 = Resistor [tolerance=±5% resistance=220 package=THT]
  VCC1 = Battery
  S1 = Pushbutton [package="[SMD]"]
  S2 = Pushbutton [package="[SMD]"]
  S3 = Pushbutton [package="[SMD]"]
  S4 = Pushbutton [package="[SMD]"]

nets:
  N1: RFduinoSMD1.gnd, RFduinoSMD1.gpio2, VCC1.-, S1.Pin_1, S1.Pin_2, S1.Pin_3, S1.Pin_4, S2.Pin_3, S2.Pin_4
  N2: RFduinoSMD1.vin, VCC1.+
  N3: RFduinoSMD1.gpio4, S3.Pin_1, S3.Pin_2, S3.Pin_3
  N4: RFduinoSMD1.gpio5, S4.Pin_3, S4.Pin_4
  N5: RFduinoSMD1.gpio6, LED1.cathode
  N6: LED1.anode, R1.Pin_1
